# Fritzing sketch PIDFritzing (saved by Fritzing 0.9.3b)
breadboards: 1

parts:
  Part1 = Arduino Uno (Rev3)
  BAT1 = Battery Holders [package=battery-aa]
  BAT2 = Battery Holders [package=battery-aa]
  BAT3 = Battery Holders [package=battery-aa]
  BAT4 = Battery Holders [package=battery-aa]
  BAT7 = Battery Holders [package=battery-aa]
  BAT8 = Battery Holders [package=battery-aa]

nets:
  N1: Part1.GND, BAT1.-
  N2: Part1.VIN, BAT3.+
  N3: BAT1.+, BAT2.-
  N4: BAT2.+, BAT8.-
  N5: BAT3.-, BAT7.+
  N6: BAT4.-, BAT8.+
  N7: BAT4.+, BAT7.-
